// Logisim project ULA-project.circ as structural Verilog: 28 circuits, main circuit main
module main (
  input  [4:0] A,
  input  [4:0] B,
  input  [2:0] C
);

  wire \controle_de_operações_da_ula_1_overflow , \controle_de_operações_da_ula_1_sinal ,
       \controle_de_operações_da_ula_1_status , display_0_1_1_a, display_0_1_1_b, display_0_1_1_c,
       display_0_1_1_d, display_0_1_1_e, display_0_1_1_f, display_0_1_1_g, display_0_9_1_a, display_0_9_1_b,
       display_0_9_1_c, display_0_9_1_d, display_0_9_1_e, display_0_9_1_f, display_0_9_1_g;
  wire [4:0] a_1_s, \controle_de_operações_da_ula_1_s ;

  LED SINAL (.in(\controle_de_operações_da_ula_1_sinal ));
  LED OVERFLOW (.in(\controle_de_operações_da_ula_1_overflow ));
  LED STATUS (.in(\controle_de_operações_da_ula_1_status ));
  \controle_de_operações_da_ULA  \controle_de_operações_da_ula_1  (
    .A(A), .B(B), .SINAL(\controle_de_operações_da_ula_1_sinal ),
    .OVERFLOW(\controle_de_operações_da_ula_1_overflow ), .STATUS(\controle_de_operações_da_ula_1_status ),
    .S(\controle_de_operações_da_ula_1_s ), .CONTROLE(C));
  A a_1 (.A(\controle_de_operações_da_ula_1_s ), .S(a_1_s));  // open: OVERFLOW, SINAL, STATUS
  display_0_1 display_0_1_1 (
    .VALOR(a_1_s), .A(display_0_1_1_a), .B(display_0_1_1_b), .C(display_0_1_1_c), .D(display_0_1_1_d),
    .E(display_0_1_1_e), .F(display_0_1_1_f), .G(display_0_1_1_g));
  _7_Segment_Display u_7_segment_display_1 (
    .g(display_0_1_1_g), .f(display_0_1_1_f), .a(display_0_1_1_a), .b(display_0_1_1_b), .e(display_0_1_1_e),
    .d(display_0_1_1_d), .c(display_0_1_1_c), .dp(1'b0));
  _7_Segment_Display u_7_segment_display_2 (
    .g(display_0_9_1_g), .f(display_0_9_1_f), .a(display_0_9_1_a), .b(display_0_9_1_b), .e(display_0_9_1_e),
    .d(display_0_9_1_d), .c(display_0_9_1_c), .dp(1'b0));
  display_0_9 display_0_9_1 (
    .VALOR(a_1_s), .A(display_0_9_1_a), .B(display_0_9_1_b), .C(display_0_9_1_c), .D(display_0_9_1_d),
    .E(display_0_9_1_e), .F(display_0_9_1_f), .G(display_0_9_1_g));
endmodule

module \controle_de_operações_da_ULA  (
  input  [2:0] CONTROLE,
  input  [4:0] A,
  input  [4:0] B,
  output SINAL,
  output OVERFLOW,
  output STATUS,
  output [4:0] S
);

  wire a_1_overflow, a_1_sinal, a_1_status, a_2_1_overflow, a_2_1_sinal, a_2_1_status, a_b_1_overflow,
       a_b_1_sinal, a_b_1_status, a_b_2_1_overflow, a_b_2_1_sinal, a_b_2_1_status, a_b_2_overflow,
       a_b_2_sinal, a_b_2_status, a_b_3_overflow, a_b_3_sinal, a_b_3_status, a_b_4_overflow, a_b_4_sinal,
       a_b_4_status, max_a_b_1_overflow, max_a_b_1_sinal, max_a_b_1_status;
  wire [4:0] a_1_s, a_2_1_s, a_b_1_s, a_b_2_1_s, a_b_2_s, a_b_3_s, a_b_4_s, max_a_b_1_s;

  A___B a_b_1 (.A(A), .B(B), .S(a_b_1_s), .SINAL(a_b_1_sinal), .STATUS(a_b_1_status), .OVERFLOW(a_b_1_overflow));
  A___B_2 a_b_2 (.A(A), .B(B), .S(a_b_2_s), .SINAL(a_b_2_sinal), .STATUS(a_b_2_status), .OVERFLOW(a_b_2_overflow));
  MAX_A_B max_a_b_1 (
    .A(A), .B(B), .S(max_a_b_1_s), .SINAL(max_a_b_1_sinal), .OVERFLOW(max_a_b_1_overflow),
    .STATUS(max_a_b_1_status));
  A____B_2_2_2_2 a_b_3 (
    .A(A), .B(B), .STATUS(a_b_3_status), .S(a_b_3_s), .OVERFLOW(a_b_3_overflow), .SINAL(a_b_3_sinal));
  A___B__2 a_b_2_1 (
    .A(A), .B(B), .STATUS(a_b_2_1_status), .S(a_b_2_1_s), .OVERFLOW(a_b_2_1_overflow), .SINAL(a_b_2_1_sinal));
  A_2 a_2_1 (.A(A), .OVERFLOW(a_2_1_overflow), .S(a_2_1_s), .SINAL(a_2_1_sinal), .STATUS(a_2_1_status));
  A a_1 (.A(A), .S(a_1_s), .OVERFLOW(a_1_overflow), .SINAL(a_1_sinal), .STATUS(a_1_status));
  A____B_2_2_2_2_2 a_b_4 (
    .A(A), .B(B), .S(a_b_4_s), .SINAL(a_b_4_sinal), .OVERFLOW(a_b_4_overflow), .STATUS(a_b_4_status));
  mux_8_1___1_bit u_SINAL (
    .ENTRADA(a_b_1_sinal), .ENTRADA_2(a_b_2_sinal), .ENTRADA_3(max_a_b_1_sinal), .ENTRADA_4(a_b_3_sinal),
    .out_10(SINAL), .ENTRADA_5(a_b_2_1_sinal), .ENTRADA_6(a_2_1_sinal), .ENTRADA_7(a_1_overflow),
    .ENTRADA_8(a_b_4_sinal), .C(CONTROLE));
  mux_8_1___1_bit u_OVERFLOW (
    .ENTRADA(a_b_1_overflow), .ENTRADA_2(a_b_2_overflow), .ENTRADA_3(max_a_b_1_overflow),
    .ENTRADA_4(a_b_3_overflow), .out_10(OVERFLOW), .ENTRADA_5(a_b_2_1_overflow), .ENTRADA_6(a_2_1_overflow),
    .ENTRADA_7(a_1_sinal), .ENTRADA_8(a_b_4_overflow), .C(CONTROLE));
  mux_8_1___1_bit u_STATUS (
    .ENTRADA(a_b_1_status), .ENTRADA_2(a_b_2_status), .ENTRADA_3(max_a_b_1_status), .ENTRADA_4(a_b_3_status),
    .out_10(STATUS), .ENTRADA_5(a_b_2_1_status), .ENTRADA_6(a_2_1_status), .ENTRADA_7(a_1_status),
    .ENTRADA_8(a_b_4_status), .C(CONTROLE));
  mux_8_1___5_bits \SAÍDA  (
    .INPUT(a_b_1_s), .INPUT_2(a_b_2_s), .INPUT_3(max_a_b_1_s), .INPUT_4(a_b_3_s), .INPUT_5(a_b_2_1_s),
    .INPUT_6(a_2_1_s), .INPUT_7(a_1_s), .INPUT_8(a_b_4_s), .S(S), .C(CONTROLE));
endmodule

module display_0_1 (
  input  [4:0] VALOR,
  output A,
  output B,
  output C,
  output D,
  output E,
  output F,
  output G
);

  wire and_1_out, and_2_out, and_3_out, and_4_out;

  and and_1 (and_1_out, ~VALOR[2], ~VALOR[1]);  // AND_Gate
  and and_2 (and_2_out, ~VALOR[2], ~VALOR[1]);  // AND_Gate
  and and_3 (and_3_out, ~VALOR[2], ~VALOR[1]);  // AND_Gate
  and and_4 (and_4_out, ~VALOR[2], ~VALOR[1]);  // AND_Gate
  or or_1 (A, ~VALOR[3], and_1_out);  // OR_Gate
  or or_2 (D, ~VALOR[3], and_2_out);  // OR_Gate
  or or_3 (E, ~VALOR[3], and_3_out);  // OR_Gate
  or or_4 (F, ~VALOR[3], and_4_out);  // OR_Gate

  assign B = 1'b1;
  assign C = 1'b1;
  assign G = 1'b0;
endmodule

module display_0_9 (
  input  [4:0] VALOR,
  output A,
  output B,
  output C,
  output D,
  output E,
  output F,
  output G
);

  wire and_1_out, and_2_out, and_3_out, and_4_out, and_5_out, and_6_out, and_7_out, and_8_out, and_9_out,
       and_10_out, and_11_out, and_12_out, and_13_out, and_14_out, and_15_out, and_16_out, and_17_out,
       and_18_out, and_19_out, and_20_out, and_21_out, and_22_out, and_23_out, and_24_out, and_25_out,
       and_26_out, and_27_out, and_28_out, and_29_out, and_30_out, and_31_out, not_1_out;

  and and_1 (and_1_out, ~VALOR[3], VALOR[1]);  // AND_Gate
  and and_2 (and_2_out, VALOR[2], VALOR[0]);
  and and_3 (and_3_out, VALOR[3], ~VALOR[1]);  // AND_Gate
  and and_4 (and_4_out, ~VALOR[2], ~VALOR[0]);  // AND_Gate
  not not_1 (not_1_out, VALOR[2]);
  and and_5 (and_5_out, ~VALOR[1], ~VALOR[0]);  // AND_Gate
  and and_6 (and_6_out, VALOR[3], ~VALOR[1]);  // AND_Gate
  and and_7 (and_7_out, VALOR[3], ~VALOR[0]);  // AND_Gate
  and and_8 (and_8_out, ~VALOR[3], VALOR[1], VALOR[0]);  // AND_Gate
  and and_9 (and_9_out, VALOR[3], ~VALOR[2]);  // AND_Gate
  and and_10 (and_10_out, ~VALOR[3], ~VALOR[1]);  // AND_Gate
  and and_11 (and_11_out, VALOR[2], VALOR[1]);
  and and_12 (and_12_out, VALOR[3], ~VALOR[1]);  // AND_Gate
  and and_13 (and_13_out, ~VALOR[2], ~VALOR[0]);  // AND_Gate
  and and_14 (and_14_out, ~VALOR[3], VALOR[1], ~VALOR[0]);  // AND_Gate
  and and_15 (and_15_out, VALOR[2], ~VALOR[1], VALOR[0]);  // AND_Gate
  and and_16 (and_16_out, VALOR[3], VALOR[2], VALOR[0]);
  and and_17 (and_17_out, ~VALOR[3], ~VALOR[2], VALOR[1]);  // AND_Gate
  and and_18 (and_18_out, ~VALOR[2], ~VALOR[0]);  // AND_Gate
  and and_19 (and_19_out, ~VALOR[3], VALOR[1], ~VALOR[0]);  // AND_Gate
  and and_20 (and_20_out, VALOR[3], ~VALOR[1], ~VALOR[0]);  // AND_Gate
  and and_21 (and_21_out, ~VALOR[3], VALOR[2], ~VALOR[1]);  // AND_Gate
  and and_22 (and_22_out, VALOR[3], VALOR[2], VALOR[1]);
  and and_23 (and_23_out, VALOR[3], ~VALOR[2], ~VALOR[1]);  // AND_Gate
  and and_24 (and_24_out, ~VALOR[2], ~VALOR[1], ~VALOR[0]);  // AND_Gate
  and and_25 (and_25_out, VALOR[2], VALOR[1], ~VALOR[0]);  // AND_Gate
  and and_26 (and_26_out, VALOR[3], VALOR[1], ~VALOR[0]);  // AND_Gate
  and and_27 (and_27_out, VALOR[3], VALOR[2]);
  and and_28 (and_28_out, VALOR[2], ~VALOR[1]);  // AND_Gate
  and and_29 (and_29_out, VALOR[2], ~VALOR[0]);  // AND_Gate
  and and_30 (and_30_out, VALOR[3], ~VALOR[1]);  // AND_Gate
  and and_31 (and_31_out, ~VALOR[3], ~VALOR[2], VALOR[1]);  // AND_Gate
  or or_1 (A, and_1_out, and_2_out, and_3_out, and_4_out);
  or or_2 (B, not_1_out, and_5_out, and_6_out, and_7_out, and_8_out);
  or or_3 (C, VALOR[0], and_9_out, and_10_out, and_11_out);
  or or_4 (D, and_12_out, and_13_out, and_14_out, and_15_out, and_16_out, and_17_out);
  or or_5 (E, and_18_out, and_19_out, and_20_out);
  or or_6 (F, and_21_out, and_22_out, and_23_out, and_24_out, and_25_out, and_26_out);
  or or_7 (G, and_27_out, and_28_out, and_29_out, and_30_out, and_31_out);
endmodule

module complemento_de_2 (
  input  [4:0] A,
  output [4:0] S
);

  wire [4:0] not_1_out;

  assign not_1_out = ~A;  // NOT_Gate not_1, 5 bits wide
  A___B a_b_1 (.A(not_1_out), .B(5'b00001), .S(S));  // open: SINAL, STATUS, OVERFLOW
endmodule

module mux_2_1___1_bit (
  input  A,
  input  B,
  input  Controle,
  output S
);

  wire and_1_out, and_2_out, not_1_out;

  not not_1 (not_1_out, Controle);
  and and_1 (and_1_out, A, not_1_out);
  and and_2 (and_2_out, B, Controle);
  or or_1 (S, and_1_out, and_2_out);
endmodule

module mux_4_1___1_bit (
  input  A,
  input  B,
  input  C,
  input  D,
  input  C1,
  input  C2,
  output S
);

  wire and_1_out, and_2_out, and_3_out, and_4_out;

  and and_1 (and_1_out, A, ~C1, ~C2);  // AND_Gate
  and and_2 (and_2_out, B, ~C1, C2);  // AND_Gate
  and and_3 (and_3_out, C, C1, ~C2);  // AND_Gate
  and and_4 (and_4_out, D, C1, C2);
  or or_1 (S, and_1_out, and_2_out, and_3_out, and_4_out);
endmodule

module mux_8_1___1_bit (
  input  ENTRADA,
  input  ENTRADA_2,
  input  ENTRADA_3,
  input  ENTRADA_4,
  input  ENTRADA_5,
  input  ENTRADA_6,
  input  ENTRADA_7,
  input  ENTRADA_8,
  input  [2:0] C,
  output out_10
);

  wire and_1_out, and_2_out, and_3_out, and_4_out, and_5_out, and_6_out, and_7_out, and_8_out;

  and and_1 (and_1_out, ENTRADA, ~C[2], ~C[1], ~C[0]);  // AND_Gate
  and and_2 (and_2_out, ENTRADA_2, ~C[2], ~C[1], C[0]);  // AND_Gate
  and and_3 (and_3_out, ENTRADA_3, ~C[2], C[1], ~C[0]);  // AND_Gate
  and and_4 (and_4_out, ENTRADA_4, ~C[2], C[1], C[0]);  // AND_Gate
  and and_5 (and_5_out, ENTRADA_5, C[2], ~C[1], ~C[0]);  // AND_Gate
  and and_6 (and_6_out, ENTRADA_6, C[2], ~C[1], C[0]);  // AND_Gate
  and and_7 (and_7_out, ENTRADA_7, C[2], C[1], ~C[0]);  // AND_Gate
  and and_8 (and_8_out, ENTRADA_8, C[2], C[1], C[0]);
  or or_1 (out_10, and_1_out, and_2_out, and_3_out, and_4_out, and_5_out, and_6_out, and_7_out, and_8_out);
endmodule

module mux_2_1___5_bits (
  input  [4:0] A,
  input  [4:0] B,
  input  CONTROLE,
  output [4:0] S
);

  mux_2_1___1_bit mux_2_1_1_bit_1 (.A(A[0]), .B(B[0]), .S(S[0]), .Controle(CONTROLE));
  mux_2_1___1_bit mux_2_1_1_bit_2 (.A(A[1]), .B(B[1]), .S(S[1]), .Controle(CONTROLE));
  mux_2_1___1_bit mux_2_1_1_bit_3 (.A(A[2]), .B(B[2]), .S(S[2]), .Controle(CONTROLE));
  mux_2_1___1_bit mux_2_1_1_bit_4 (.A(A[3]), .B(B[3]), .S(S[3]), .Controle(CONTROLE));
  mux_2_1___1_bit mux_2_1_1_bit_5 (.A(A[4]), .B(B[4]), .S(S[4]), .Controle(CONTROLE));
endmodule

module mux_8_1___5_bits (
  input  [2:0] C,
  input  [4:0] INPUT,
  input  [4:0] INPUT_2,
  input  [4:0] INPUT_3,
  input  [4:0] INPUT_4,
  input  [4:0] INPUT_5,
  input  [4:0] INPUT_6,
  input  [4:0] INPUT_7,
  input  [4:0] INPUT_8,
  output [4:0] S
);

  mux_8_1___1_bit mux_8_1_1_bit_1 (
    .ENTRADA(INPUT[0]), .ENTRADA_2(INPUT_2[0]), .ENTRADA_3(INPUT_3[0]), .ENTRADA_4(INPUT_4[0]),
    .out_10(S[0]), .ENTRADA_5(INPUT_5[0]), .ENTRADA_6(INPUT_6[0]), .ENTRADA_7(INPUT_7[0]),
    .ENTRADA_8(INPUT_8[0]), .C(C));
  mux_8_1___1_bit mux_8_1_1_bit_2 (
    .ENTRADA(INPUT[1]), .ENTRADA_2(INPUT_2[1]), .ENTRADA_3(INPUT_3[1]), .ENTRADA_4(INPUT_4[1]),
    .out_10(S[1]), .ENTRADA_5(INPUT_5[1]), .ENTRADA_6(INPUT_6[1]), .ENTRADA_7(INPUT_7[1]),
    .ENTRADA_8(INPUT_8[1]), .C(C));
  mux_8_1___1_bit mux_8_1_1_bit_3 (
    .ENTRADA(INPUT[2]), .ENTRADA_2(INPUT_2[2]), .ENTRADA_3(INPUT_3[2]), .ENTRADA_4(INPUT_4[2]),
    .out_10(S[2]), .ENTRADA_5(INPUT_5[2]), .ENTRADA_6(INPUT_6[2]), .ENTRADA_7(INPUT_7[2]),
    .ENTRADA_8(INPUT_8[2]), .C(C));
  mux_8_1___1_bit mux_8_1_1_bit_4 (
    .ENTRADA(INPUT[3]), .ENTRADA_2(INPUT_2[3]), .ENTRADA_3(INPUT_3[3]), .ENTRADA_4(INPUT_4[3]),
    .out_10(S[3]), .ENTRADA_5(INPUT_5[3]), .ENTRADA_6(INPUT_6[3]), .ENTRADA_7(INPUT_7[3]),
    .ENTRADA_8(INPUT_8[3]), .C(C));
  mux_8_1___1_bit mux_8_1_1_bit_5 (
    .ENTRADA(INPUT[4]), .ENTRADA_2(INPUT_2[4]), .ENTRADA_3(INPUT_3[4]), .ENTRADA_4(INPUT_4[4]),
    .out_10(S[4]), .ENTRADA_5(INPUT_5[4]), .ENTRADA_6(INPUT_6[4]), .ENTRADA_7(INPUT_7[4]),
    .ENTRADA_8(INPUT_8[4]), .C(C));
endmodule

module A___B_1_bit (
  input  Carry_in,
  input  A,
  input  B,
  output S,
  output Carry_out
);

  wire and_1_out, and_2_out, xor_1_out;

  xor xor_1 (xor_1_out, A, B);
  and and_1 (and_1_out, A, B);
  xor xor_2 (S, Carry_in, xor_1_out);
  and and_2 (and_2_out, xor_1_out, Carry_in);
  or or_1 (Carry_out, and_2_out, and_1_out);
endmodule

module A___B_1_bit_2 (
  input  A,
  input  B,
  output S
);

  and and_1 (S, ~A, B);  // AND_Gate
endmodule

module A___B_1_bit_2_2 (
  input  A,
  input  B,
  output S
);

  xnor xnor_1 (S, A, B);
endmodule

module A____B (
  input  [4:0] A,
  input  [4:0] B,
  output S
);

  wire a_b_1_bit_1_s, a_b_1_bit_2_s, a_b_1_bit_3_s, a_b_1_bit_4_s, a_b_1_bit_5_s, a_b_1_bit_6_s,
       a_b_1_bit_7_s, a_b_1_bit_8_s, a_b_1_bit_9_s, a_b_1_bit_10_s, and_1_out, and_2_out, and_3_out,
       and_4_out, and_5_out;

  A___B_1_bit_2 a_b_1_bit_1 (.A(A[4]), .B(B[4]), .S(a_b_1_bit_1_s));
  A___B_1_bit_2_2 a_b_1_bit_2 (.A(A[4]), .B(B[4]), .S(a_b_1_bit_2_s));
  A___B_1_bit_2 a_b_1_bit_3 (.A(A[3]), .B(B[3]), .S(a_b_1_bit_3_s));
  A___B_1_bit_2_2 a_b_1_bit_4 (.A(A[3]), .B(B[3]), .S(a_b_1_bit_4_s));
  A___B_1_bit_2 a_b_1_bit_5 (.A(A[2]), .B(B[2]), .S(a_b_1_bit_5_s));
  A___B_1_bit_2_2 a_b_1_bit_6 (.A(A[2]), .B(B[2]), .S(a_b_1_bit_6_s));
  A___B_1_bit_2 a_b_1_bit_7 (.A(A[1]), .B(B[1]), .S(a_b_1_bit_7_s));
  A___B_1_bit_2_2 a_b_1_bit_8 (.A(A[1]), .B(B[1]), .S(a_b_1_bit_8_s));
  A___B_1_bit_2 a_b_1_bit_9 (.A(A[0]), .B(B[0]), .S(a_b_1_bit_9_s));
  A___B_1_bit_2_2 a_b_1_bit_10 (.A(A[0]), .B(B[0]), .S(a_b_1_bit_10_s));
  and and_1 (and_1_out, a_b_1_bit_2_s, a_b_1_bit_3_s);
  and and_2 (and_2_out, a_b_1_bit_2_s, a_b_1_bit_4_s, a_b_1_bit_5_s);
  and and_3 (and_3_out, a_b_1_bit_2_s, a_b_1_bit_4_s, a_b_1_bit_6_s, a_b_1_bit_7_s);
  and and_4 (and_4_out, a_b_1_bit_2_s, a_b_1_bit_4_s, a_b_1_bit_6_s, a_b_1_bit_8_s, a_b_1_bit_9_s);
  and and_5 (and_5_out, a_b_1_bit_2_s, a_b_1_bit_4_s, a_b_1_bit_6_s, a_b_1_bit_8_s, a_b_1_bit_10_s);
  or or_1 (S, a_b_1_bit_1_s, and_1_out, and_2_out, and_3_out, and_4_out, and_5_out);
endmodule

module A____B_2 (
  input  [4:0] A,
  input  [4:0] B,
  output out_3
);


  assign out_3 = 1'b0;
endmodule

module A____B_2_2 (
  input  [4:0] A,
  input  [4:0] B,
  output out_3
);


  assign out_3 = 1'b1;
endmodule

module A____B_2_2_2 (
  input  [4:0] in_1,
  input  [4:0] in_2,
  output out_3
);

  wire a_b_1_s;
  wire [4:0] a_1_s, a_2_s;

  A a_1 (.A(in_1), .S(a_1_s));  // open: OVERFLOW, SINAL, STATUS
  A a_2 (.A(in_2), .S(a_2_s));  // open: OVERFLOW, SINAL, STATUS
  not not_1 (out_3, a_b_1_s);
  A____B a_b_1 (.A(a_1_s), .B(a_2_s), .S(a_b_1_s));
endmodule

module decoder_A____B (
  input  A2,
  input  A1,
  input  A0,
  output S1,
  output S2,
  output S3,
  output S4,
  output S5
);

  wire and_1_out, and_2_out, and_3_out;

  and and_1 (and_1_out, A1, A0);
  and and_2 (and_2_out, A2, A0);
  and and_3 (and_3_out, A2, A1);
  or or_1 (S1, A2, A1, A0);
  or or_2 (S2, A2, A1);
  or or_3 (S3, and_1_out, A2);
  or or_4 (S5, and_2_out, and_3_out);

  assign S4 = A2;
endmodule

module decoder_A_2 (
  input  A1,
  input  A0,
  output [4:0] S
);

  wire not_1_out;

  not not_1 (not_1_out, A0);
  and and_1 (S[3], A1, A0);
  and and_2 (S[2], A1, not_1_out);

  assign {S[4], S[1:0]} = {2'b00, A0};
endmodule

module A____1 (
  input  [4:0] A,
  input  in_2,
  output [4:0] S
);

  wire not_1_out;

  mux_2_1___5_bits mux_2_1_5_bits_1 (.A({1'b0, A[4:1]}), .B(A), .CONTROLE(not_1_out), .S(S));
  not not_1 (not_1_out, in_2);
endmodule

module A___B (
  input  [4:0] A,
  input  [4:0] B,
  output [4:0] S,
  output SINAL,
  output STATUS,
  output OVERFLOW
);

  wire a_b_1_bit_1_s, a_b_1_bit_2_s, a_b_1_bit_4_carry_out, a_b_1_bit_5_carry_out, a_b_1_bit_6_carry_out,
       a_b_1_bit_7_carry_out;

  A___B_1_bit_2_2 a_b_1_bit_1 (.A(A[4]), .B(B[4]), .S(a_b_1_bit_1_s));
  A___B_1_bit_2_2 a_b_1_bit_2 (.A(B[4]), .B(S[4]), .S(a_b_1_bit_2_s));
  A___B_1_bit a_b_1_bit_3 (.Carry_in(a_b_1_bit_4_carry_out), .A(A[4]), .B(B[4]), .S(S[4]));  // open: Carry_out
  nand nand_1 (OVERFLOW, a_b_1_bit_1_s, a_b_1_bit_2_s);
  A___B_1_bit a_b_1_bit_4 (
    .Carry_in(a_b_1_bit_5_carry_out), .A(A[3]), .B(B[3]), .S(S[3]), .Carry_out(a_b_1_bit_4_carry_out));
  A___B_1_bit a_b_1_bit_5 (
    .Carry_in(a_b_1_bit_6_carry_out), .A(A[2]), .B(B[2]), .S(S[2]), .Carry_out(a_b_1_bit_5_carry_out));
  A___B_1_bit a_b_1_bit_6 (
    .Carry_in(a_b_1_bit_7_carry_out), .A(A[1]), .B(B[1]), .S(S[1]), .Carry_out(a_b_1_bit_6_carry_out));
  A___B_1_bit a_b_1_bit_7 (.Carry_in(1'b0), .A(A[0]), .B(B[0]), .S(S[0]), .Carry_out(a_b_1_bit_7_carry_out));

  assign SINAL = S[4];
  assign STATUS = 1'b0;
endmodule

module A___B_2 (
  input  [4:0] A,
  input  [4:0] B,
  output [4:0] S,
  output SINAL,
  output STATUS,
  output OVERFLOW
);

  wire a_b_1_bit_1_s, a_b_1_bit_2_s, not_1_out, not_2_out;
  wire [4:0] complemento_de_2_1_s;

  A___B_1_bit_2_2 a_b_1_bit_1 (.A(A[4]), .B(B[4]), .S(a_b_1_bit_1_s));
  A___B_1_bit_2_2 a_b_1_bit_2 (.A(S[4]), .B(A[4]), .S(a_b_1_bit_2_s));
  complemento_de_2 complemento_de_2_1 (.A(B), .S(complemento_de_2_1_s));
  not not_1 (not_1_out, a_b_1_bit_1_s);
  not not_2 (not_2_out, a_b_1_bit_2_s);
  and and_1 (OVERFLOW, not_1_out, not_2_out);
  A___B a_b_1 (.A(A), .B(complemento_de_2_1_s), .S(S), .SINAL(SINAL), .STATUS(STATUS));  // open: OVERFLOW
endmodule

module MAX_A_B (
  input  [4:0] A,
  input  [4:0] B,
  output [4:0] S,
  output SINAL,
  output OVERFLOW,
  output STATUS
);

  wire a_b_1_status;

  A____B_2_2_2_2 a_b_1 (.A(A), .B(B), .STATUS(a_b_1_status));  // open: S, OVERFLOW, SINAL
  mux_2_1___5_bits mux_2_1_5_bits_1 (.A(A), .B(B), .CONTROLE(a_b_1_status), .S(S));

  assign OVERFLOW = 1'b0;
  assign SINAL = S[4];
  assign STATUS = 1'b0;
endmodule

module A____B_2_2_2_2 (
  input  [4:0] A,
  input  [4:0] B,
  output STATUS,
  output [4:0] S,
  output SINAL,
  output OVERFLOW
);

  wire a_b_1_s, a_b_2_out_3, a_b_3_out_3, a_b_4_out_3;

  A____B a_b_1 (.A(A), .B(B), .S(a_b_1_s));
  A____B_2 a_b_2 (.A(A), .B(B), .out_3(a_b_2_out_3));
  A____B_2_2 a_b_3 (.A(A), .B(B), .out_3(a_b_3_out_3));
  A____B_2_2_2 a_b_4 (.in_1(A), .in_2(B), .out_3(a_b_4_out_3));
  mux_4_1___1_bit mux_4_1_1_bit_1 (
    .A(a_b_1_s), .B(a_b_2_out_3), .C(a_b_3_out_3), .D(a_b_4_out_3), .S(STATUS), .C1(A[4]), .C2(B[4]));

  assign OVERFLOW = 1'b0;
  assign S = {5{1'b0}};
  assign SINAL = 1'b0;
endmodule

module A___B__2 (
  input  [4:0] A,
  input  [4:0] B,
  output [4:0] S,
  output SINAL,
  output STATUS,
  output OVERFLOW
);

  wire a_b_2_status;
  wire [4:0] a_b_1_s;

  A___B a_b_1 (.A(A), .B(B), .S(a_b_1_s), .STATUS(STATUS));  // open: SINAL, OVERFLOW
  A____1 a_1_1 (.A(a_b_1_s), .S(S), .in_2(1'b1));
  A____B_2_2_2_2 a_b_2 (.A(S), .B(5'b01111), .STATUS(a_b_2_status));  // open: S, OVERFLOW, SINAL
  not not_1 (OVERFLOW, a_b_2_status);

  assign SINAL = S[4];
endmodule

module A_2 (
  input  [4:0] A,
  output OVERFLOW,
  output [4:0] S,
  output SINAL,
  output STATUS
);

  wire [4:0] a_1_s;

  A a_1 (.A(A), .S(a_1_s));  // open: OVERFLOW, SINAL, STATUS
  decoder_A_2 decoder_a_2_1 (.A1(a_1_s[1]), .A0(a_1_s[0]), .S(S));
  or or_1 (OVERFLOW, a_1_s[4], a_1_s[3], a_1_s[2]);

  assign SINAL = 1'b0;
  assign STATUS = 1'b0;
endmodule

module A (
  input  [4:0] A,
  output [4:0] S,
  output OVERFLOW,
  output SINAL,
  output STATUS
);

  wire [4:0] xor_5_out;

  xor xor_1 (xor_5_out[4], A[4], A[4]);
  xor xor_2 (xor_5_out[3], A[4], A[3]);
  xor xor_3 (xor_5_out[2], A[4], A[2]);
  xor xor_4 (xor_5_out[1], A[4], A[1]);
  xor xor_5 (xor_5_out[0], A[4], A[0]);
  A___B a_b_1 (.A(xor_5_out), .B({4'b0000, A[4]}), .S(S), .SINAL(OVERFLOW));  // open: STATUS, OVERFLOW

  assign SINAL = 1'b0;
  assign STATUS = 1'b0;
endmodule

module A____B_2_2_2_2_2 (
  input  [4:0] A,
  input  [4:0] B,
  output [4:0] S,
  output SINAL,
  output OVERFLOW,
  output STATUS
);

  wire decoder_a_b_1_s1, decoder_a_b_1_s2, decoder_a_b_1_s3, decoder_a_b_1_s4, decoder_a_b_1_s5;
  wire [4:0] a_1_1_s, a_1_2_s, a_1_3_s, a_1_4_s, a_1_5_s;
  wire [4:4] nor_1_out;

  decoder_A____B decoder_a_b_1 (
    .S1(decoder_a_b_1_s1), .S2(decoder_a_b_1_s2), .S3(decoder_a_b_1_s3), .S4(decoder_a_b_1_s4),
    .S5(decoder_a_b_1_s5), .A2(B[2]), .A1(B[1]), .A0(B[0]));
  A____1 a_1_1 (.A(A), .S(a_1_1_s), .in_2(decoder_a_b_1_s1));
  A____1 a_1_2 (.A(a_1_1_s), .S(a_1_2_s), .in_2(decoder_a_b_1_s2));
  nor nor_1 (nor_1_out[4], B[3], B[4]);
  A____1 a_1_3 (.A(a_1_4_s), .S(a_1_3_s), .in_2(decoder_a_b_1_s4));
  A____1 a_1_4 (.A(a_1_2_s), .S(a_1_4_s), .in_2(decoder_a_b_1_s3));
  A____1 a_1_5 (.A(a_1_3_s), .S(a_1_5_s), .in_2(decoder_a_b_1_s5));
  assign S = a_1_5_s & {5{nor_1_out[4]}};  // AND_Gate and_1, 5 bits wide

  assign OVERFLOW = 1'b0;
  assign SINAL = 1'b0;
  assign STATUS = 1'b0;
endmodule
